# Fritzing sketch ardutester_v113_otPu7eBf45 (saved by Fritzing 0.9.3b)
breadboards: 1

parts:
  LCD1 = LCD screen
  TEST = Pushbutton [package="[THT]"]
  part = Arduino Uno (Rev3)
  R1 = Resistor [tolerance=±1% resistance=680 package=THT]
  R2 = Resistor [tolerance=±1% resistance=680 package=THT]
  R3 = Resistor [tolerance=±1% resistance=680 package=THT]
  R4 = Resistor [tolerance=±1% resistance=470k package=THT]
  R5 = Resistor [tolerance=±1% resistance=470k package=THT]
  R6 = Resistor [tolerance=±1% resistance=470k package=THT]
  R7 = Resistor [tolerance=±5% resistance=1k package=THT]
  R8 = Resistor [tolerance=±5% resistance=10k package=THT]

nets:
  GND: LCD1.VSS, LCD1.R/W, LCD1.LED-, TEST.Pin_1, TEST.Pin_2, part.GND, R7.Pin_0
  5V: LCD1.VDD, part.5V, R8.Pin_1
  N1: LCD1.V0, R7.Pin_1
  N2: LCD1.RS, part.D7
  N3: LCD1.E, part.D6_PWM
  N4: LCD1.DB4, part.D5_PWM
  N5: LCD1.DB5, part.D4
  N6: LCD1.DB6, part.D3_PWM
  N7: LCD1.DB7, part.D2
  3.3V: LCD1.LED+, part.3V3
  N8: TEST.Pin_3, TEST.Pin_4, part.A3, R8.Pin_0
  TP1: part.A0, R1.Pin_1, R4.Pin_0
  TP2: part.A1, R2.Pin_1, R5.Pin_0
  TP3: part.A2, R3.Pin_1, R6.Pin_0
  N9: part.D8, R1.Pin_0
  N10: part.D9_PWM, R4.Pin_1
  N11: part.D10_PWM/SS, R2.Pin_0
  N12: part.D11_PWM/MOSI, R5.Pin_1
  N13: part.D12/MISO, R3.Pin_0
  N14: part.D13/SCK, R6.Pin_1
